# Fritzing sketch PumpenwacheV2 (saved by Fritzing 0.9.4)
breadboards: 1

parts:
  WeMos_D1_Mini1 = WeMos D1 Mini
  ACS712 = ACS712 Low Current Sensor Board v12
  BME280 = BME280 Breakout

nets:
  3V3: WeMos_D1_Mini1.3V3, BME280.3.3V
  5V: WeMos_D1_Mini1.5V, ACS712.5V
  N1: WeMos_D1_Mini1.A0, ACS712.VO
  N2: WeMos_D1_Mini1.D1, BME280.SCK/SCL
  N3: WeMos_D1_Mini1.D2, BME280.SDI/SDA
  GND: WeMos_D1_Mini1.G, ACS712.GND, BME280.GND
